# Fritzing sketch PiSwitch Main Components (saved by Fritzing 1.0.5)

parts:
  Raspberry_Pi_1 = Raspberry Pi 3 [part_number=RPI-3-V1.2]
  Part1 = Adafruit Stereo 2.8W Class D Audio Amplifier - I2C Control AGC - TPA2016 [part_number="Adafruit #1712"]
  BATT1 = LiPoly Battery (1300mAh)
  SPK_R = SPEAKER [package=pcb_mount_speaker]
  SPK_L = SPEAKER [package=pcb_mount_speaker]
  Adafruit_PCM510x_I2S_DAC1 = Adafruit PCM510x I2S DAC [part_number=#6250]

nets:
  3V3: Raspberry_Pi_1.3v3, Raspberry_Pi_1.3V3, Part1.I2C_VCC
  N1: Raspberry_Pi_1.GPIO2, Part1.SDA
  N2: Raspberry_Pi_1.GPIO3, Part1.SCL
  N3: Raspberry_Pi_1.GIPO19, Adafruit_PCM510x_I2S_DAC1.WORDSEL_IN
  N4: Raspberry_Pi_1.GIPO21, Adafruit_PCM510x_I2S_DAC1.DATA_IN
  GND: Raspberry_Pi_1.GND, Part1.GND, Part1.IN_R_N, Part1.IN_L_N, BATT1.negative, Adafruit_PCM510x_I2S_DAC1.AGND
  N5: Raspberry_Pi_1.GIPO18, Adafruit_PCM510x_I2S_DAC1.BITCLK_IN
  N6: Raspberry_Pi_1.GIPO15, Part1.SHUTDOWN
  5V: Raspberry_Pi_1.5V, Part1.VDD, BATT1.positive, Adafruit_PCM510x_I2S_DAC1.VIN
  N7: Part1.OUT_L_N, SPK_L.-
  N8: Part1.OUT_L_P, SPK_L.+
  N9: Part1.OUT_R_P, SPK_R.+
  N10: Part1.OUT_R_N, SPK_R.-
  N11: Part1.IN_R_P, Adafruit_PCM510x_I2S_DAC1.OUTR
  N12: Part1.IN_L_P, Adafruit_PCM510x_I2S_DAC1.OUTL

custom parts:
  Adafruit Stereo 2.8W Class D Audio Amplifier - I2C Control AGC - TPA2016: A mini class D with AGC and I2C control? Yes please! This incredibly small stereo amplifier is surprisingly powerful. It is able to deliver 2 x 2.8W channels into 4 ohm impedance speakers (@ 10% THD) and it has a i2c control interface as well as an AGC (automatic gain control) system to keep your audio from clipping or distorting. If you don't want to use I2C to control it, it does start up on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
  LiPoly Battery (1300mAh): Lithium Ion Polymer Battery (1300mAh)
  Adafruit PCM510x I2S DAC: We stock a lot of chips and development boards that are able to do high quality digital I2S out, which makes for great quality audio playback. That's great when you have enough processing power to decode WAVs or MP3s in real time. However, we don't have a good selection of I2S DAC boards...until now! We really love the sounds coming out of the Adafruit PCM5102 I2S DAC with Line Level Output -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
