# Fritzing sketch Unified controller (saved by Fritzing 1.0.5)
circuit board: 20.3218cm x 10.2647cm

parts:
  D-Pad_Down = Pushbutton [package="[THT]"]
  D-Pad_Right = Pushbutton [package="[THT]"]
  D-Pad_Up = Pushbutton [package="[THT]"]
  D-Pad_Left = Pushbutton [package="[THT]"]
  BT-ShoulderRight = Pushbutton [package="[THT]"]
  BT-X = Pushbutton [package="[THT]"]
  BT-B = Pushbutton [package="[THT]"]
  BT-Y = Pushbutton [package="[THT]"]
  BT-Start = Pushbutton [package="[THT]"]
  BT-ShoulderLeft = Pushbutton [package="[THT]"]
  BT-Select = Pushbutton [package="[THT]"]
  V1 = DC Power [voltage=3.3V internal_resistance=0.1Ω max_current=0.1A]
  Trigger-Left = POT [knob_status=0% power=0.5W package=alps_pot]
  Trigger-Right = POT [knob_status=25% power=0.5W package=alps_pot]
  Central_MCU = Itsy Bitsy M0 Express
  BT-A = Pushbutton [package="[THT]"]
  Joystick-Left = Thumb Joystick [package=joystick]
  U2 = Thumb Joystick [package=joystick]

nets:
  GND: D-Pad_Down.Pin_1, D-Pad_Down.Pin_2, D-Pad_Right.Pin_1, D-Pad_Right.Pin_2, D-Pad_Up.Pin_1, D-Pad_Up.Pin_2, D-Pad_Left.Pin_1, D-Pad_Left.Pin_2, BT-Start.Pin_1, BT-Start.Pin_2, BT-ShoulderLeft.Pin_1, BT-ShoulderLeft.Pin_2, BT-Select.Pin_1, BT-Select.Pin_2, Trigger-Left.A, Trigger-Right.A, Central_MCU.GND, Joystick-Left.SEL-, Joystick-Left.H-, Joystick-Left.V-, U2.SEL-, U2.H-, U2.V-
  N1: D-Pad_Down.Pin_3, D-Pad_Down.Pin_4, Central_MCU.SCK
  N2: D-Pad_Right.Pin_3, D-Pad_Right.Pin_4, Central_MCU.D11
  N3: D-Pad_Up.Pin_3, D-Pad_Up.Pin_4, Central_MCU.D2
  N4: D-Pad_Left.Pin_3, D-Pad_Left.Pin_4, Central_MCU.MOSI
  N5: BT-ShoulderRight.Pin_1, BT-ShoulderRight.Pin_2, BT-X.Pin_1, BT-X.Pin_2, BT-B.Pin_1, BT-B.Pin_2, BT-Y.Pin_1, BT-Y.Pin_2, BT-A.Pin_1, BT-A.Pin_2
  N6: BT-ShoulderRight.Pin_3, BT-ShoulderRight.Pin_4, Central_MCU.D10
  N7: BT-X.Pin_3, BT-X.Pin_4, Central_MCU.D4
  N8: BT-B.Pin_3, BT-B.Pin_4, Central_MCU.D9
  N9: BT-Y.Pin_3, BT-Y.Pin_4, Central_MCU.D7
  N10: BT-Start.Pin_3, BT-Start.Pin_4, Central_MCU.D0
  N11: BT-ShoulderLeft.Pin_3, BT-ShoulderLeft.Pin_4, Central_MCU.D12
  N12: BT-Select.Pin_3, BT-Select.Pin_4, Central_MCU.D13
  N13: V1.V-, Trigger-Left.E, Trigger-Right.E, Central_MCU.+3V3, U2.V+, U2.H+
  N14: V1.V+, Joystick-Left.V+, Joystick-Left.H+
  N15: Trigger-Left.S, Central_MCU.A0
  N16: Trigger-Right.S, Central_MCU.A5
  N17: Central_MCU.D3, U2.SEL+
  N18: Central_MCU.D1, BT-A.Pin_3, BT-A.Pin_4
  N19: Central_MCU.MISO, Joystick-Left.SEL+
  N20: Central_MCU.A4, U2.H
  N21: Central_MCU.A3, U2.V
  N22: Central_MCU.A2, Joystick-Left.H
  N23: Central_MCU.A1, Joystick-Left.V

custom parts:
  Itsy Bitsy M0 Express: What's smaller than a Feather but larger than a Trinket? It's an Adafruit ItsyBitsy M0 Express! Small, powerful, with a rockin' ATSAMD21 Cortex M0 processor running at 48 MHz - this microcontroller board is perfect when you want something very compact, but still with a bunch of pins. ItsyBitsy M0 Express is only 1.4" long by 0.7" wide, but has 6 power pins, 23 digital GPIO pins (12 of which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
