# Fritzing sketch Fritzing Test (saved by Fritzing 1.0.5)

parts:
  Left_Sub-MCU = Raspberry Pi Pico or Pico 2
  Raspberry_Pi_1 = Raspberry Pi 3 [part_number=RPI-3-V1.2]  # not connected
  Part1 = Adafruit Stereo 2.8W Class D Audio Amplifier - I2C Control AGC - TPA2016 [part_number="Adafruit #1712"]  # not connected
  Primary_MCU = Raspberry Pi Pico or Pico 2
  Right_Sub-MCU = Raspberry Pi Pico or Pico 2
  R1 = Resistor [tolerance=±5% power=0.25W resistance=220 package=THT]  # not connected

nets:
  N1: Left_Sub-MCU.pin_16, Primary_MCU.pin_16, Right_Sub-MCU.pin_16
  N2: Left_Sub-MCU.pin_23, Left_Sub-MCU.pin_33, Left_Sub-MCU.pin_38, Primary_MCU.pin_3, Primary_MCU.pin_33, Primary_MCU.pin_38, Primary_MCU.pin_42, Right_Sub-MCU.pin_3, Right_Sub-MCU.pin_38, Right_Sub-MCU.pin_42
  N3: Left_Sub-MCU.pin_39, Primary_MCU.pin_39, Right_Sub-MCU.pin_39

custom parts:
  Raspberry Pi Pico or Pico 2: Raspberry Pi Pico and Pico 2. Based around the RP2040 and RP2350 microcontrollers respectively, Picos are low cost microcontroller device bringing Raspberry Pi quality, cost, and easy of use to the microcontroller space. Jan 2021, Split part in to two versions: tht (this one) and SMD. This one will drill holes for a .1 in header in pcb to allow plugging in the module as well as providing pads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
  Adafruit Stereo 2.8W Class D Audio Amplifier - I2C Control AGC - TPA2016: A mini class D with AGC and I2C control? Yes please! This incredibly small stereo amplifier is surprisingly powerful. It is able to deliver 2 x 2.8W channels into 4 ohm impedance speakers (@ 10% THD) and it has a i2c control interface as well as an AGC (automatic gain control) system to keep your audio from clipping or distorting. If you don't want to use I2C to control it, it does start up on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
